# Fritzing sketch sketch (saved by Fritzing 0.9.3b)
breadboards: 1

parts:
  Componente1 = Arduino Uno (Rev3)
  R1 = Resistor [tolerance=±5% resistance=220 package=THT]
  R2 = Resistor [tolerance=±5% resistance=220 package=THT]
  R3 = Resistor [tolerance=±5% resistance=220 package=THT]
  LED1 = LED - 5mm [color="Green (560nm)" package="5 mm [THT]"]
  LED2 = LED - 5mm [color="Green (560nm)" package="5 mm [THT]"]
  LED3 = LED - 5mm [color="Green (560nm)" package="5 mm [THT]"]
  S1 = Pushbutton [package="[THT]"]
  R4 = Resistor [tolerance=±5% resistance=10k package=THT]
  LED4 = LED - 5mm [color="White (6500K)" package="5 mm [THT]"]
  R5 = Resistor [tolerance=±5% resistance=220 package=THT]
  LED5 = LED - 5mm [color="Red (635nm)" package="5 mm [THT]"]
  R6 = Resistor [tolerance=±5% resistance=220 package=THT]
  S2 = Pushbutton [package="[THT]"]
  R7 = Resistor [tolerance=±5% resistance=10k package=THT]
  R8 = Rotary Potentiometer (Small) [maximum_resistance=100kΩ package=THT]
  R9 = Resistor [tolerance=±5% resistance=220 package=THT]
  R10 = Resistor [tolerance=±5% resistance=220 package=THT]
  R11 = Resistor [tolerance=±5% resistance=220 package=THT]
  R12 = Resistor [tolerance=±5% resistance=220 package=THT]
  R13 = Resistor [tolerance=±5% resistance=220 package=THT]
  R14 = Resistor [tolerance=±5% resistance=10k package=THT]
  R15 = Resistor [tolerance=±5% resistance=10k package=THT]
  S3 = Pushbutton [package="[THT]"]
  S4 = Pushbutton [package="[THT]"]
  LED6 = LED - 5mm [color="Red (633nm)" package="5 mm [THT]"]
  LED7 = LED - 5mm [color="White (8000K)" package="5 mm [THT]"]
  LED8 = LED - 5mm [color="Green (570nm)" package="5 mm [THT]"]
  LED9 = LED - 5mm [color="Green (570nm)" package="5 mm [THT]"]
  LED10 = LED - 5mm [color="Green (570nm)" package="5 mm [THT]"]
  R16 = Rotary Potentiometer (Small) [maximum_resistance=100kΩ package=THT]

nets:
  N1: Componente1.A0, R8.wiper, R16.wiper
  N2: Componente1.D8, R3.Pin_1, R11.Pin_1
  N3: Componente1.D12/MISO, R6.Pin_1, R13.Pin_1
  N4: Componente1.D2, S1.Pin_3, S1.Pin_4, R4.Pin_1, R14.Pin_1, S3.Pin_3, S3.Pin_4
  N5: Componente1.D3_PWM, S2.Pin_3, S2.Pin_4, R7.Pin_1, R15.Pin_1, S4.Pin_3, S4.Pin_4
  N6: Componente1.D4, R1.Pin_1, R10.Pin_1
  N7: Componente1.D5_PWM, R5.Pin_1, R12.Pin_1
  N8: Componente1.D7, R2.Pin_1, R9.Pin_1
  N9: Componente1.5V, S1.Pin_1, S1.Pin_2, S2.Pin_1, S2.Pin_2, R8.leg1, S3.Pin_1, S3.Pin_2, S4.Pin_1, S4.Pin_2, R16.leg1
  N10: Componente1.GND, LED1.cathode, LED2.cathode, LED3.cathode, R4.Pin_0, LED4.cathode, LED5.cathode, R7.Pin_0, R8.leg2, R14.Pin_0, R15.Pin_0, LED6.cathode, LED7.cathode, LED8.cathode, LED9.cathode, LED10.cathode, R16.leg2
  N11: R1.Pin_0, LED3.anode, R10.Pin_0, LED10.anode
  N12: R2.Pin_0, LED2.anode, R9.Pin_0, LED9.anode
  N13: R3.Pin_0, LED1.anode, R11.Pin_0, LED8.anode
  N14: LED4.anode, R5.Pin_0, R12.Pin_0, LED7.anode
  N15: LED5.anode, R6.Pin_0, R13.Pin_0, LED6.anode
